# Fritzing sketch HandHeld (saved by Fritzing 0.9.3b)
circuit board: 6.36622cm x 2.85423cm
circuit board: 6.36622cm x 4.85236cm
breadboards: 1

parts:
  10K = Photocell (LDR) [package=THT]
  L = Momentary Switch [package=ksa_sealed_tac_switch]
  R3 = Photocell (LDR) [package=THT]
  C7 = Capacitor [package=cap-pth-small]
  L1 = Momentary Switch [package=ksa_sealed_tac_switch]
  C2 = Capacitor [package=cap-pth-small]
  10K1 = Photocell (LDR) [package=THT]
  R4 = Photocell (LDR) [package=THT]
  L2 = Momentary Switch [package=ksa_sealed_tac_switch]
  C4 = Capacitor [package=cap-pth-small]
  10K2 = Photocell (LDR) [package=THT]
  R5 = Photocell (LDR) [package=THT]
  L3 = Momentary Switch [package=ksa_sealed_tac_switch]
  C6 = Capacitor [package=cap-pth-small]
  10K3 = Photocell (LDR) [package=THT]
  R6 = Photocell (LDR) [package=THT]
  Part2 = Arduino Nano (Rev3.0) (ICSP)
  Part3 = NRF24L01+ Breakout Board

nets:
  N1: 10K.pin_0, R3.pin_1, C7.2
  N2: L.1, R3.pin_0
  N3: L.3, C7.1
  N4: L1.1, R4.pin_0
  N5: L1.3, C2.1
  N6: 10K1.pin_0, R4.pin_1
  N7: L2.1, R5.pin_0
  N8: L2.3, C4.1
  N9: C4.2, 10K2.pin_0, R5.pin_1
  N10: L3.1, R6.pin_0
  N11: L3.3, C6.1
  N12: C6.2, 10K3.pin_0, R6.pin_1
  N13: Part2.D7, Part3.CS
  N14: Part2.D10, Part3.CE
  N15: Part2.D11/MOSI, Part3.MOSI
  N16: Part2.D12/MISO, Part3.MISO
  N17: Part2.D13/SCK, Part3.SCK
